// Logisim project circuit (project2).circ as structural Verilog: 1 circuit, main circuit main
module main (
  input  P3,
  input  S3,
  input  P2,
  input  C,
  input  S2,
  input  P1,
  input  S1,
  input  P0,
  input  S0,
  input  A1,
  input  A0,
  input  U1,
  input  U0,
  output GRANT,
  output DENY,
  output D0,
  output D1,
  output D2,
  output D3
);

  wire and_1_out, and_2_out, and_3_out, and_4_out, not_1_out, not_2_out, not_3_out, xnor_1_out, xnor_2_out,
       xnor_3_out, xnor_4_out;

  xnor xnor_1 (xnor_1_out, P3, S3);
  xnor xnor_2 (xnor_2_out, P2, S2);
  xnor xnor_3 (xnor_3_out, P1, S1);
  xnor xnor_4 (xnor_4_out, P0, S0);
  and and_1 (and_1_out, A1, A0);
  and and_2 (and_2_out, xnor_1_out, xnor_2_out);
  and and_3 (and_3_out, xnor_3_out, xnor_4_out);
  not not_1 (not_1_out, and_1_out);
  and and_4 (and_4_out, and_2_out, and_3_out);
  and and_5 (GRANT, C, and_4_out, not_1_out);
  not not_2 (not_2_out, U1);
  not not_3 (not_3_out, U0);
  not not_4 (DENY, GRANT);
  and and_6 (D0, GRANT, not_2_out, not_3_out);
  and and_7 (D1, GRANT, not_2_out, U0);
  and and_8 (D2, GRANT, U1, not_3_out);
  and and_9 (D3, GRANT, U1, U0);
endmodule
