// Logisim project ddca project.circ as structural Verilog: 1 circuit, main circuit main
module main (
  input  in_1,
  input  in_2,
  input  in_3,
  input  in_4,
  output out_5,
  output out_6,
  output out_7,
  output out_8
);

  wire not_1_out, not_2_out, not_3_out, not_4_out;

  not not_1 (not_1_out, in_1);
  not not_2 (not_2_out, in_1);
  not not_3 (not_3_out, in_1);
  not not_4 (not_4_out, in_1);
  and and_1 (out_5, in_1, not_1_out);
  and and_2 (out_6, in_1, not_2_out);
  and and_3 (out_7, in_1, not_3_out);
  and and_4 (out_8, in_1, not_4_out);

  assign in_2 = in_1;
  assign in_3 = in_1;
  assign in_4 = in_1;
endmodule
